# Fritzing sketch Thermostat (saved by Fritzing 0.9.3b)
breadboards: 1

parts:
  AVR328p = Arduino Nano (Rev3.0)
  LCD = LCD screen
  R17 = Trimmer Potentiometer [maximum_resistance=10kΩ package=THT]
  Next = Pushbutton [package="[THT]"]
  C3 = Ceramic Capacitor [capacitance=0.1µF package="100 mil [THT, multilayer]"]
  Prev = Pushbutton [package="[THT]"]
  C4 = Ceramic Capacitor [capacitance=0.1µF package="100 mil [THT, multilayer]"]
  RESET = Pushbutton [package="[THT]"]
  C5 = Ceramic Capacitor [capacitance=0.1µF package="100 mil [THT, multilayer]"]
  DS1 = DS18B20 1-Wire Temperature Sensor [part_number=DS18B20]
  R18 = Resistor [tolerance=±5% resistance=4.7k package=THT]

nets:
  N1: AVR328p.D1/TX, RESET.Pin_1, RESET.Pin_2, C5.0
  N2: AVR328p.D2, Next.Pin_1, Next.Pin_2, C3.0
  N3: AVR328p.D3, Prev.Pin_1, Prev.Pin_2, C4.0
  N4: AVR328p.D4, LCD.DB7
  N5: AVR328p.D5, LCD.DB6
  N6: AVR328p.D6, LCD.DB5
  N7: AVR328p.D7, LCD.DB4
  N8: AVR328p.D8, LCD.E
  N9: AVR328p.D9, LCD.RS
  N10: AVR328p.D12/MISO, DS1.DQ, R18.Pin_0
  5V: AVR328p.5V, LCD.VDD, LCD.LED+, R17.leg1, DS1.VDD, R18.Pin_1
  GND: LCD.VSS, LCD.R/W, LCD.LED-, R17.leg2, Next.Pin_4, C3.1, Prev.Pin_3, Prev.Pin_4, C4.1, RESET.Pin_3, RESET.Pin_4, C5.1, DS1.GND
  N11: LCD.V0, R17.wiper
